# Fritzing sketch MCButtonsAND (saved by Fritzing 0.8.3b)
breadboards: 1

parts:
  S1 = Momentary Switch [package=ksa_sealed_tac_switch]
  S2 = Momentary Switch [package=ksa_sealed_tac_switch]
  LED1 = Red LED-R - 3mm [package="T1.75 (3mm)"]
  R1 = Resistor [tolerance=±5% resistance=220 package=THT]
  BAT1 = Battery Holders [package=battcom_20mm_pth]

nets:
  N1: S1.4, BAT1.-
  N2: S2.2, LED1.cathode
  N3: R1.Pin_1, BAT1.+

custom parts:
  Red LED-R - 3mm: A generic red LED (~1.8V)
