# Fritzing sketch MCDIPSwitchesAND (saved by Fritzing 0.8.3b)
breadboards: 1

parts:
  LED1 = Red LED-R - 3mm [package="T1.75 (3mm)"]
  R1 = Resistor [tolerance=±5% resistance=220 package=THT]
  SW1 = DIP SWITCH [package=dipswitch-02]
  VCC1 = 4 x AAA Battery Mount

nets:
  N1: LED1.cathode, SW1.3
  N2: R1.Pin_1, VCC1.-
  N3: SW1.1, VCC1.+
  N4: SW1.2, SW1.4

custom parts:
  Red LED-R - 3mm: A generic red LED (~1.8V)
