# Fritzing sketch MCSwitchesOR (saved by Fritzing 0.8.3b)
breadboards: 1

parts:
  LED1 = Red LED-R - 3mm [package="T1.75 (3mm)"]
  R1 = Resistor [tolerance=±5% resistance=220 package=THT]
  BAT1 = Battery Holders [package=battcom_20mm_pth]
  S1 = Toggle Switch [package=THT]
  S2 = Toggle Switch [package=THT]

nets:
  N1: LED1.cathode, S1.L2, S2.L2
  N2: R1.Pin_1, BAT1.+
  N3: BAT1.-, S1.COM, S2.COM

custom parts:
  Red LED-R - 3mm: A generic red LED (~1.8V)
