# Fritzing sketch MineCraftRLCircuitOR (saved by Fritzing 0.8.5b)
breadboards: 1

parts:
  R1 = Resistor [tolerance=±5% resistance=10k package=THT]
  R2 = Resistor [tolerance=±5% resistance=10k package=THT]
  R3 = Resistor [tolerance=±5% resistance=10k package=THT]
  R4 = Resistor [tolerance=±5% resistance=10k package=THT]
  R5 = Resistor [tolerance=±5% resistance=1k package=THT]
  R6 = Resistor [tolerance=±5% resistance=1k package=THT]
  R7 = Resistor [tolerance=±5% resistance=1k package=THT]
  R8 = Resistor [tolerance=±5% resistance=1k package=THT]
  R9 = Resistor [tolerance=±5% resistance=220 package=THT]
  LED1 = LED - 5mm [color="Red (633nm)" package="5 mm [THT]"]
  LED2 = LED - 5mm [color="Red (633nm)" package="5 mm [THT]"]
  R10 = Resistor [tolerance=±5% resistance=220 package=THT]
  R11 = Resistor [tolerance=±5% resistance=220 package=THT]
  VCC1 = Battery
  Q4 = NPN-Transistor [package="TO92 [THT]"]
  Q6 = NPN-Transistor [package="TO92 [THT]"]
  Q1 = NPN-Transistor [package="TO92 [THT]"]
  Q5 = NPN-Transistor [package="TO92 [THT]"]
  Q2 = NPN-Transistor [package="TO92 [THT]"]
  Q3 = NPN-Transistor [package="TO92 [THT]"]

nets:
  N1: R1.Pin_0, Q1.B
  N2: R1.Pin_1, Q2.C
  N3: R2.Pin_0, Q3.B
  N4: R2.Pin_1, Q4.C
  N5: R3.Pin_0, R7.Pin_0, Q1.E
  N6: R3.Pin_1, R4.Pin_1, R5.Pin_1, R6.Pin_1, R9.Pin_1, VCC1.+, Q6.C, Q5.C
  N7: R4.Pin_0, R8.Pin_0, Q3.E
  N8: R5.Pin_0, Q2.E
  N9: R6.Pin_0, Q4.E
  N10: R7.Pin_1, Q5.B
  N11: R8.Pin_1, Q6.B
  N12: R9.Pin_0, LED1.anode, Q6.E, Q5.E
  N13: LED1.cathode, R10.Pin_0
  N14: LED2.cathode, R11.Pin_0
  N15: R10.Pin_1, R11.Pin_1, VCC1.-, Q1.C, Q3.C

notes:
  INPUTS are Touch Switches
