# Fritzing sketch MineCraftRL-Torch (saved by Fritzing 0.7.12b)
breadboards: 1

parts:
  Q1 = NPN-Transistor [package="TO92 [THT]"]
  VCC1 = 4 x AAA Battery Mount
  LED1 = LED - 5mm [color="Red (633nm)" package="5 mm [THT]"]
  R1 = Resistor [tolerance=±5% resistance=220 package=THT]
  R2 = Resistor [tolerance=±5% resistance=220 package=THT]

nets:
  N1: Q1.E, R1.Pin_1
  N2: Q1.B, VCC1.+, LED1.cathode
  N3: Q1.C, R2.Pin_0
  N4: VCC1.-, R2.Pin_1
  N5: LED1.anode, R1.Pin_0
