# Fritzing sketch MineCraftRLCircuitOR (saved by Fritzing 0.7.12b)
breadboards: 1

parts:
  Q1 = NPN-Transistor [package="TO92 [THT]"]
  Q2 = NPN-Transistor [package="TO92 [THT]"]
  Q3 = NPN-Transistor [package="TO92 [THT]"]
  Q4 = NPN-Transistor [package="TO92 [THT]"]
  Q5 = NPN-Transistor [package="TO92 [THT]"]
  Q6 = NPN-Transistor [package="TO92 [THT]"]
  R1 = Resistor [tolerance=±5% resistance=10k package=THT]
  R2 = Resistor [tolerance=±5% resistance=10k package=THT]
  R3 = Resistor [tolerance=±5% resistance=10k package=THT]
  R4 = Resistor [tolerance=±5% resistance=10k package=THT]
  R5 = Resistor [tolerance=±5% resistance=1k package=THT]
  R6 = Resistor [tolerance=±5% resistance=1k package=THT]
  R7 = Resistor [tolerance=±5% resistance=1k package=THT]
  R8 = Resistor [tolerance=±5% resistance=1k package=THT]
  R9 = Resistor [tolerance=±5% resistance=220 package=THT]
  LED1 = LED - 5mm [color="Red (633nm)" package="5 mm [THT]"]
  LED2 = LED - 5mm [color="Red (633nm)" package="5 mm [THT]"]
  R10 = Resistor [tolerance=±5% resistance=220 package=THT]
  R11 = Resistor [tolerance=±5% resistance=220 package=THT]
  VCC1 = Battery

nets:
  N1: Q1.E, R3.Pin_0, R7.Pin_0
  N2: Q1.B, R1.Pin_0
  N3: Q1.C, Q3.C, R10.Pin_1, R11.Pin_1, VCC1.-
  N4: Q2.E, R5.Pin_0
  N5: Q2.C, R1.Pin_1
  N6: Q3.E, R4.Pin_0, R8.Pin_0
  N7: Q3.B, R2.Pin_0
  N8: Q4.E, R6.Pin_0
  N9: Q4.C, R2.Pin_1
  N10: Q5.E, Q6.E, R9.Pin_0, LED1.anode
  N11: Q5.B, R7.Pin_1
  N12: Q5.C, Q6.C, R3.Pin_1, R4.Pin_1, R5.Pin_1, R6.Pin_1, R9.Pin_1, VCC1.+
  N13: Q6.B, R8.Pin_1
  N14: LED1.cathode, R10.Pin_0
  N15: LED2.cathode, R11.Pin_0

notes:
  INPUTS are Touch Switches
