# Fritzing sketch MinecraftRLANDgate (saved by Fritzing 0.8.5b)
breadboards: 1

parts:
  R1 = Resistor [tolerance=±5% resistance=10k package=THT]
  R2 = Resistor [tolerance=±5% resistance=10k package=THT]
  R3 = Resistor [tolerance=±5% resistance=4.7k package=THT]
  LED1 = LED - 5mm [color="Red (633nm)" package="5 mm [THT]"]
  S1 = Pushbutton [package="[THT]"]
  S2 = Pushbutton [package="[THT]"]
  Q1 = NPN-Transistor [package="TO92 [THT]"]
  Q2 = NPN-Transistor [package="TO92 [THT]"]

nets:
  N1: R1.Pin_0, S1.Pin_1, S1.Pin_2
  N2: R1.Pin_1, Q1.B
  N3: R2.Pin_0, S2.Pin_1, S2.Pin_2
  N4: R2.Pin_1, Q2.B
  N5: R3.Pin_0, LED1.anode
  N6: R3.Pin_1, Q1.E
  N7: S1.Pin_3, S1.Pin_4
  N8: S2.Pin_3, S2.Pin_4
  N9: Q1.C, Q2.E
