# Fritzing sketch MinecraftRLORgate (saved by Fritzing 0.8.5b)
breadboards: 1

parts:
  VCC1 = 4 x AAA Battery Mount
  R1 = Resistor [tolerance=±5% resistance=10k package=THT]
  R2 = Resistor [tolerance=±5% resistance=10k package=THT]
  LED1 = LED - 5mm [color="Red (633nm)" package="5 mm [THT]"]
  R3 = Resistor [tolerance=±5% resistance=220 package=THT]
  R4 = Resistor [tolerance=±5% resistance=220 package=THT]  # not connected
  R5 = Resistor [tolerance=±5% resistance=220 package=THT]
  Q2 = NPN-Transistor [package="TO92 [THT]"]
  Q1 = NPN-Transistor [package="TO92 [THT]"]

nets:
  N1: VCC1.-, R3.Pin_0
  N2: VCC1.+, Q2.C, Q1.C
  GND: R1.Pin_1, LED1.cathode, R3.Pin_1, Q1.B
  N3: R2.Pin_1, Q2.B
  N4: LED1.anode, R5.Pin_0
  N5: R5.Pin_1, Q2.E, Q1.E
