# Fritzing sketch Transitor-and-mini_bb (saved by Fritzing 0.8.5b)
breadboards: 1

parts:
  S1 = Pushbutton [package="[THT]"]
  S2 = Pushbutton [package="[THT]"]
  VCC1 = Battery
  R1 = Resistor [tolerance=±5% resistance=10k package=THT]
  R2 = Resistor [tolerance=±5% resistance=10k package=THT]
  LED1 = LED - 5mm [color="Red (633nm)" package="5 mm [THT]"]
  R3 = Resistor [tolerance=±5% resistance=220 package=THT]
  Q1 = NPN-Transistor [package="TO92 [THT]"]
  Q2 = NPN-Transistor [package="TO92 [THT]"]
  R4 = Resistor [tolerance=±5% resistance=4.7k package=THT]

nets:
  N1: S1.Pin_1, S1.Pin_2, R1.Pin_0
  N2: S1.Pin_3, S1.Pin_4, S2.Pin_3, S2.Pin_4, VCC1.+
  N3: S2.Pin_1, S2.Pin_2, R2.Pin_0
  N4: VCC1.-, R3.Pin_1, R4.Pin_1
  N5: R1.Pin_1, Q1.B
  N6: R2.Pin_1, Q2.B
  N7: LED1.cathode, R3.Pin_0
  N8: LED1.anode, Q2.C, R4.Pin_0
  N9: Q1.C, Q2.E
