# Fritzing sketch Transitor-or-mini_bb (saved by Fritzing 0.8.5b)
breadboards: 1

parts:
  S1 = Pushbutton [package="[THT]"]
  S2 = Pushbutton [package="[THT]"]
  Q4 = NPN-Transistor [package="TO92 [THT]"]
  VCC1 = Battery
  R1 = Resistor [tolerance=±5% resistance=10k package=THT]
  R2 = Resistor [tolerance=±5% resistance=10k package=THT]
  LED1 = LED - 5mm [color="Red (633nm)" package="5 mm [THT]"]
  R3 = Resistor [tolerance=±5% resistance=220 package=THT]
  Q6 = NPN-Transistor [package="TO92 [THT]"]

nets:
  N1: S1.Pin_1, S1.Pin_2, R1.Pin_0
  N2: S1.Pin_3, S1.Pin_4, Q4.C, VCC1.+, Q6.C
  N3: S2.Pin_1, S2.Pin_2, R2.Pin_0
  N4: S2.Pin_3, S2.Pin_4
  N5: Q4.E, R3.Pin_0, Q6.E
  N6: Q4.B, R2.Pin_1
  N7: VCC1.-, LED1.cathode
  N8: R1.Pin_1, Q6.B
  N9: LED1.anode, R3.Pin_1
