# Fritzing sketch Transitor-setup-mini_bb (saved by Fritzing 0.8.5b)
breadboards: 2

parts:
  S1 = Pushbutton [package="[THT]"]
  S2 = Pushbutton [package="[THT]"]
  Q3 = NPN-Transistor [package="TO92 [THT]"]
  VCC1 = Battery
  LED1 = LED - 5mm [color="Red (633nm)" package="5 mm [THT]"]
  Q5 = NPN-Transistor [package="TO92 [THT]"]

nets:
  N1: S1.Pin_1, S1.Pin_2
  N2: S1.Pin_3, S1.Pin_4, VCC1.+
  N3: S2.Pin_1, S2.Pin_2
  N4: S2.Pin_3, S2.Pin_4
  N5: Q3.E, Q5.E
  N6: Q3.C, Q5.C
  N7: VCC1.-, LED1.cathode
