# Fritzing sketch transitor-or-breakout-mini-bb (saved by Fritzing 0.8.5b)
breadboards: 1

parts:
  Q4 = NPN-Transistor [package="TO92 [THT]"]
  Q6 = NPN-Transistor [package="TO92 [THT]"]

nets:
  N1: Q4.E, Q6.E
  N2: Q4.C, Q6.C
