# Fritzing sketch NAND-AND (saved by Fritzing 0.8.5b)
breadboards: 2

parts:
  S1 = Pushbutton [package="[THT]"]
  S2 = Pushbutton [package="[THT]"]
  LED1 = LED - 5mm [color="Red (633nm)" package="5 mm [THT]"]
  U1 = 74HC595 [package="DIP16 [THT]"]
  U2 = 74HC595 [package="DIP16 [THT]"]
  R1 = Resistor [tolerance=±5% resistance=10k package=THT]
  R2 = Resistor [tolerance=±5% resistance=10k package=THT]
  R3 = Resistor [tolerance=±5% resistance=220 package=THT]
  LED2 = LED - 5mm [color="Red (633nm)" package="5 mm [THT]"]
  R4 = Resistor [tolerance=±5% resistance=220 package=THT]
  R5 = Resistor [tolerance=±5% resistance=220 package=THT]
  R6 = Resistor [tolerance=±5% resistance=220 package=THT]

nets:
  N1: S1.Pin_1, S1.Pin_2, U1.Q5, R1.Pin_0
  N2: S1.Pin_3, S1.Pin_4, S2.Pin_3, S2.Pin_4, R5.Pin_0, R6.Pin_0
  N3: S2.Pin_1, S2.Pin_2, U1.Q6, R2.Pin_0
  N4: LED1.cathode, R3.Pin_0
  N5: U1.Q1, U1.Q2, U1.Q7
  N6: U1.Q3, LED2.anode
  GND: U1.GND, U2.GND, R3.Pin_1, R4.Pin_1
  N7: U1.VCC, R5.Pin_1
  N8: U2.VCC, R6.Pin_1
  N9: R1.Pin_1, R2.Pin_1
  N10: LED2.cathode, R4.Pin_0
