# Fritzing sketch NAND-FullADDR (saved by Fritzing 0.8.5b)
breadboards: 2

parts:
  S1 = Pushbutton [package="[THT]"]
  S2 = Pushbutton [package="[THT]"]
  LED1 = LED - 5mm [color="Red (633nm)" package="5 mm [THT]"]
  U1 = 74HC595 [package="DIP16 [THT]"]
  R1 = Resistor [tolerance=±5% resistance=10k package=THT]
  R2 = Resistor [tolerance=±5% resistance=10k package=THT]
  R3 = Resistor [tolerance=±5% resistance=220 package=THT]
  LED2 = LED - 5mm [color="Red (633nm)" package="5 mm [THT]"]
  R4 = Resistor [tolerance=±5% resistance=220 package=THT]
  R5 = Resistor [tolerance=±5% resistance=220 package=THT]
  R6 = Resistor [tolerance=±5% resistance=220 package=THT]
  U2 = 74HC595 [package="DIP16 [THT]"]
  Q1 = NPN-Transistor [package="TO92 [THT]"]
  Q2 = NPN-Transistor [package="TO92 [THT]"]
  R7 = Resistor [tolerance=±5% resistance=4.7k package=THT]

nets:
  N1: S1.Pin_1, S1.Pin_2, U1.Q1, U1.Q0, R1.Pin_0
  N2: S1.Pin_3, S1.Pin_4, S2.Pin_3, S2.Pin_4, R5.Pin_0, R6.Pin_0, R7.Pin_0
  N3: S2.Pin_1, S2.Pin_2, U1.Q2, U1.SH_CP, R2.Pin_0
  N4: LED1.cathode, R3.Pin_0, U2.Q7
  N5: U1.Q3, U1.MR, U1.DS, Q1.B
  N6: U1.Q5, U1.OE
  N7: U1.Q6, U1.Q7'
  N8: U1.Q7, U2.Q1, U2.Q0
  GND: U1.GND, R3.Pin_1, R4.Pin_1, U2.GND, Q2.C
  N9: U1.VCC, R5.Pin_1
  N10: R1.Pin_1, R2.Pin_1
  N11: LED2.cathode, R4.Pin_0
  N12: LED2.anode, Q1.E, R7.Pin_1
  N13: R6.Pin_1, U2.VCC
  N14: U2.Q2, U2.SH_CP
  N15: U2.Q3, U2.DS, Q2.B
  N16: U2.Q5, U2.OE
  N17: U2.Q6, U2.Q7'
  N18: Q1.C, Q2.E
