# Fritzing sketch TRANSITOR-OR (saved by Fritzing 0.8.5b)
breadboards: 2

parts:
  S1 = Pushbutton [package="[THT]"]
  S2 = Pushbutton [package="[THT]"]
  LED1 = LED - 5mm [color="Red (633nm)" package="5 mm [THT]"]
  R1 = Resistor [tolerance=±5% resistance=10k package=THT]
  R2 = Resistor [tolerance=±5% resistance=10k package=THT]
  R3 = Resistor [tolerance=±5% resistance=220 package=THT]
  LED2 = LED - 5mm [color="Red (633nm)" package="5 mm [THT]"]
  R4 = Resistor [tolerance=±5% resistance=220 package=THT]
  Q5 = NPN-Transistor [package="TO92 [THT]"]
  Q6 = NPN-Transistor [package="TO92 [THT]"]

nets:
  N1: S1.Pin_1, S1.Pin_2, R1.Pin_0, Q5.B
  N2: S1.Pin_3, S1.Pin_4, S2.Pin_3, S2.Pin_4
  N3: S2.Pin_1, S2.Pin_2, R2.Pin_0
  N4: LED1.cathode, R3.Pin_0
  N5: R1.Pin_1, R2.Pin_1
  N6: R3.Pin_1, R4.Pin_1
  N7: LED2.cathode, R4.Pin_0
  N8: LED2.anode, Q5.C, Q6.C
  N9: Q5.E, Q6.E
